# Fritzing sketch Untitled Sketch (saved by Fritzing 0.9.6b)
breadboards: 1

parts:
  INA1 = INA219 DC Current Sensor Breakout
  M1 = Niren can bus module [package=THT]
  Part1 = Arduino Nano Every

nets:
  VCC: INA1.VCC, M1.pin1, M1.pin5, Part1.D11/MOSI, Part1.+5V
  GND: INA1.GND, M1.pin2, M1.pin6, Part1.GND, Part1.D13~
  N1: INA1.SCL, Part1.A5
  N2: INA1.SDA, Part1.A4
  N3: M1.pin3, Part1.D10~
  N4: M1.pin4, Part1.D12~/MISO
  N5: M1.pin7, Part1.D2
  N6: Part1.RESET, Part1.A7

custom parts:
  INA219 DC Current Sensor Breakout: INA DC Current Sensor Breakout
  Niren can bus module: Niren can bus module availabe on ebay and others. Pcb view assumes that you unsolder the 7 pin header and resolder it on the bottom of the module to connect to the pcb. The two jumpers and the can bus connector remain on the top of the board and don't appear in pcb view.
  Arduino Nano Every: The Nano Every is Arduino’s 5V compatible board in the smallest available form factor: 45x18mm! The Arduino Nano is the preferred board for many projects requiring a small and easy to use microcontroller board. The small footprint and low price, make the Nano Every particularly suited for wearable inventions, low cost robotics, electronic musical instruments, and general use to control smaller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
